// Logisim project Pong_LEDMatrix.circ as structural Verilog: 5 circuits, main circuit main
module main (
  input  reset,
  input  in_2,
  input  in_3,
  input  [3:0] in_4,
  input  [3:0] in_5,
  input  in_6,
  input  [9:0] in_7,
  output [9:0] out_8
);

  wire button_1_out, button_2_out, button_3_out, clock_1_out, collision_detector_1_out_3;
  wire [3:0] ball_logic_1_out_8, ball_logic_1_out_9;
  wire [9:0] or_1_out, pixel_flusher_1_line_1, pixel_flusher_1_line_2, pixel_flusher_1_line_3,
       pixel_flusher_1_line_4, pixel_flusher_1_line_5, pixel_flusher_1_line_6, pixel_flusher_1_line_7,
       pixel_flusher_1_line_8, pixel_flusher_1_line_9, pixel_flusher_1_line_10;

  Clock clock_1 (.out(clock_1_out));
  Button button_1 (.out(button_1_out));
  Button button_2 (.out(button_2_out));
  Button button_3 (.out(button_3_out));
  ball_logic ball_logic_1 (
    .clk(clock_1_out), .start(button_3_out), .reset(reset), .load(in_3), .input_x(in_4), .input_y(in_5),
    .collide(collision_detector_1_out_3), .out_8(ball_logic_1_out_8), .out_9(ball_logic_1_out_9));
  collision_detector collision_detector_1 (
    .in_1(out_8), .in_2(pixel_flusher_1_line_9), .out_3(collision_detector_1_out_3));
  pixel_flusher pixel_flusher_1 (
    .en(in_2), .col(ball_logic_1_out_8), .row(ball_logic_1_out_9), .Line_1(pixel_flusher_1_line_1),
    .Line_2(pixel_flusher_1_line_2), .Line_3(pixel_flusher_1_line_3), .Line_4(pixel_flusher_1_line_4),
    .Line_5(pixel_flusher_1_line_5), .Line_6(pixel_flusher_1_line_6), .Line_7(pixel_flusher_1_line_7),
    .Line_8(pixel_flusher_1_line_8), .Line_9(pixel_flusher_1_line_9), .Line_10(pixel_flusher_1_line_10));
  LR_SHREG_10BIT lr_shreg_10bit_1 (
    .shR(button_1_out), .shL(button_2_out), .load(in_6), .clk(clock_1_out), .data(in_7), .reset(reset),
    .dataout(out_8));
  assign or_1_out = pixel_flusher_1_line_10 | out_8;  // OR_Gate or_1, 10 bits wide
  DotMatrix #(.inputtype("row"), .matrixcols(10), .matrixrows(10)) dotmatrix_1 (
    .row0(pixel_flusher_1_line_1), .row1(pixel_flusher_1_line_2), .row2(pixel_flusher_1_line_3),
    .row3(pixel_flusher_1_line_4), .row4(pixel_flusher_1_line_5), .row5(pixel_flusher_1_line_6),
    .row6(pixel_flusher_1_line_7), .row7(pixel_flusher_1_line_8), .row8(pixel_flusher_1_line_9),
    .row9(or_1_out));
endmodule

module pixel_flusher (
  input  en,
  input  [3:0] col,
  input  [3:0] row,
  output [9:0] Line_1,
  output [9:0] Line_2,
  output [9:0] Line_3,
  output [9:0] Line_4,
  output [9:0] Line_5,
  output [9:0] Line_6,
  output [9:0] Line_7,
  output [9:0] Line_8,
  output [9:0] Line_9,
  output [9:0] Line_10
);

  wire [9:0] decoder_1_out0;

  Decoder #(.select(4)) decoder_1 (
    .out0(decoder_1_out0[0]), .out1(decoder_1_out0[1]), .out2(decoder_1_out0[2]), .out3(decoder_1_out0[3]),
    .out4(decoder_1_out0[4]), .out5(decoder_1_out0[5]), .out6(decoder_1_out0[6]), .out7(decoder_1_out0[7]),
    .out8(decoder_1_out0[8]), .out9(decoder_1_out0[9]), .sel(col), .en(en));  // open: out10, out11, out12, out13, out14, out15
  Demultiplexer #(.select(4), .width(10)) demultiplexer_1 (
    .out0(Line_1), .out1(Line_2), .out2(Line_3), .out3(Line_4), .out4(Line_5), .out5(Line_6), .out6(Line_7),
    .out7(Line_8), .out8(Line_9), .out9(Line_10), .in(decoder_1_out0), .sel(row));  // open: out10, out11, out12, out13, out14, out15
endmodule

module LR_SHREG_10BIT (
  input  shR,
  input  shL,
  input  load,
  input  clk,
  input  [9:0] data,
  input  reset,
  output [9:0] dataout
);

  wire multiplexer_1_out, multiplexer_2_out, multiplexer_3_out, multiplexer_4_out, multiplexer_5_out,
       multiplexer_6_out, multiplexer_7_out, multiplexer_8_out, multiplexer_9_out, multiplexer_10_out;
  wire [1:0] priority_encoder_1_out;

  Priority_Encoder #(.select(2)) priority_encoder_1 (
    .in0(1'b1), .in1(shR), .in2(shL), .in3(load), .out(priority_encoder_1_out), .en_in(1'b1));  // open: gs, en_out
  Multiplexer #(.select(2)) multiplexer_1 (
    .in0(dataout[0]), .in1(dataout[1]), .in2(dataout[9]), .in3(data[0]), .out(multiplexer_1_out),
    .sel(priority_encoder_1_out));
  Multiplexer #(.select(2)) multiplexer_2 (
    .in0(dataout[1]), .in1(dataout[2]), .in2(dataout[0]), .in3(data[1]), .out(multiplexer_2_out),
    .sel(priority_encoder_1_out));
  Multiplexer #(.select(2)) multiplexer_3 (
    .in0(dataout[2]), .in1(dataout[3]), .in2(dataout[1]), .in3(data[2]), .out(multiplexer_3_out),
    .sel(priority_encoder_1_out));
  Multiplexer #(.select(2)) multiplexer_4 (
    .in0(dataout[3]), .in1(dataout[4]), .in2(dataout[2]), .in3(data[3]), .out(multiplexer_4_out),
    .sel(priority_encoder_1_out));
  Multiplexer #(.select(2)) multiplexer_5 (
    .in0(dataout[4]), .in1(dataout[5]), .in2(dataout[3]), .in3(data[4]), .out(multiplexer_5_out),
    .sel(priority_encoder_1_out));
  Multiplexer #(.select(2)) multiplexer_6 (
    .in0(dataout[5]), .in1(dataout[6]), .in2(dataout[4]), .in3(data[5]), .out(multiplexer_6_out),
    .sel(priority_encoder_1_out));
  Multiplexer #(.select(2)) multiplexer_7 (
    .in0(dataout[6]), .in1(dataout[7]), .in2(dataout[5]), .in3(data[6]), .out(multiplexer_7_out),
    .sel(priority_encoder_1_out));
  Multiplexer #(.select(2)) multiplexer_8 (
    .in0(dataout[7]), .in1(dataout[8]), .in2(dataout[6]), .in3(data[7]), .out(multiplexer_8_out),
    .sel(priority_encoder_1_out));
  Multiplexer #(.select(2)) multiplexer_9 (
    .in0(dataout[8]), .in1(dataout[9]), .in2(dataout[7]), .in3(data[8]), .out(multiplexer_9_out),
    .sel(priority_encoder_1_out));
  Multiplexer #(.select(2)) multiplexer_10 (
    .in0(dataout[9]), .in1(dataout[0]), .in2(dataout[8]), .in3(data[9]), .out(multiplexer_10_out),
    .sel(priority_encoder_1_out));
  D_Flip_Flop d_ff_1 (.D(multiplexer_1_out), .clk(clk), .Q(dataout[0]), .reset(reset));  // open: Qn, preset
  D_Flip_Flop d_ff_2 (.D(multiplexer_2_out), .clk(clk), .Q(dataout[1]), .reset(reset));  // open: Qn, preset
  D_Flip_Flop d_ff_3 (.D(multiplexer_3_out), .clk(clk), .Q(dataout[2]), .reset(reset));  // open: Qn, preset
  D_Flip_Flop d_ff_4 (.D(multiplexer_4_out), .clk(clk), .Q(dataout[3]), .reset(reset));  // open: Qn, preset
  D_Flip_Flop d_ff_5 (.D(multiplexer_5_out), .clk(clk), .Q(dataout[4]), .reset(reset));  // open: Qn, preset
  D_Flip_Flop d_ff_6 (.D(multiplexer_6_out), .clk(clk), .Q(dataout[5]), .reset(reset));  // open: Qn, preset
  D_Flip_Flop d_ff_7 (.D(multiplexer_7_out), .clk(clk), .Q(dataout[6]), .reset(reset));  // open: Qn, preset
  D_Flip_Flop d_ff_8 (.D(multiplexer_8_out), .clk(clk), .Q(dataout[7]), .reset(reset));  // open: Qn, preset
  D_Flip_Flop d_ff_9 (.D(multiplexer_9_out), .clk(clk), .Q(dataout[8]), .reset(reset));  // open: Qn, preset
  D_Flip_Flop d_ff_10 (.D(multiplexer_10_out), .clk(clk), .Q(dataout[9]), .reset(reset));  // open: Qn, preset

  // Notes on the sheet:
  //   Currently Only SHIFT RIGHT is Working
  //   0 -> no effect / state save
  //   1 -> shift left
  //   2 -> shift right
  //   3 -> parallel load
endmodule

module ball_logic (
  input  clk,
  input  start,
  input  reset,
  input  load,
  input  [3:0] input_x,
  input  [3:0] input_y,
  input  collide,
  output [3:0] out_8,
  output [3:0] out_9
);

  wire comparator_1_eq, comparator_1_lt, comparator_2_eq, comparator_3_eq, comparator_3_lt, comparator_4_eq,
       or_1_out, or_2_out, or_3_out, s_r_ff_1_q, s_r_ff_2_q;

  Comparator #(.mode("unsigned"), .width(4)) comparator_1 (
    .a(out_8), .b(4'b0001), .eq(comparator_1_eq), .lt(comparator_1_lt));  // open: gt
  Comparator #(.mode("unsigned"), .width(4)) comparator_2 (
    .a(out_8), .b(4'b1000), .eq(comparator_2_eq));  // open: gt, lt
  Comparator #(.mode("unsigned"), .width(4)) comparator_3 (
    .a(out_9), .b(4'b0001), .eq(comparator_3_eq), .lt(comparator_3_lt));  // open: gt
  Comparator #(.mode("unsigned"), .width(4)) comparator_4 (
    .a(out_9), .b(4'b1000), .eq(comparator_4_eq));  // open: gt, lt
  or or_1 (or_1_out, comparator_1_lt, comparator_1_eq);
  or or_2 (or_2_out, comparator_3_lt, comparator_3_eq);
  S_R_Flip_Flop s_r_ff_1 (
    .S(or_1_out), .R(comparator_2_eq), .clk(clk), .Q(s_r_ff_1_q), .reset(reset), .preset(start));  // open: Qn
  S_R_Flip_Flop s_r_ff_2 (
    .S(or_2_out), .R(comparator_4_eq), .clk(clk), .Q(s_r_ff_2_q), .reset(or_3_out), .preset(start));  // open: Qn
  or or_3 (or_3_out, collide, reset);
  Counter #(.max('hf), .width(4)) X (
    .clr(reset), .load(load), .up(s_r_ff_1_q), .clk(clk), .D(input_x), .Q(out_8));  // open: count, carry
  Counter #(.max('hf), .width(4)) Y (
    .clr(reset), .load(load), .up(s_r_ff_2_q), .clk(clk), .D(input_y), .Q(out_9));  // open: count, carry
  Bit_Extender #(.in_width(4), .out_width(10), .\type ("zero")) bit_extender_1 ();  // open: in, out
endmodule

module collision_detector (
  input  [9:0] in_1,
  input  [9:0] in_2,
  output out_3
);

  wire comparator_1_eq;
  wire [9:0] and_1_out;

  assign and_1_out = in_1 & in_2;  // AND_Gate and_1, 10 bits wide
  not not_1 (out_3, comparator_1_eq);
  Comparator #(.mode("unsigned"), .width(10)) comparator_1 (
    .a(and_1_out), .b({10{1'b0}}), .eq(comparator_1_eq));  // open: gt, lt
endmodule
